# Fritzing sketch binary_clock (saved by Fritzing 0.9.3b)
breadboards: 1

parts:
  Composant1 = Arduino Uno (Rev3)
  LED1 = LED - 5mm [color="Red (633nm)" package="5 mm [THT]"]
  LED2 = LED - 5mm [color="Red (633nm)" package="5 mm [THT]"]
  LED3 = LED - 5mm [color="Red (633nm)" package="5 mm [THT]"]
  LED4 = LED - 5mm [color="Red (633nm)" package="5 mm [THT]"]
  LED5 = LED - 5mm [color="Red (633nm)" package="5 mm [THT]"]
  LED6 = LED - 5mm [color="Red (633nm)" package="5 mm [THT]"]
  LED7 = LED - 5mm [color="Red (633nm)" package="5 mm [THT]"]
  LED8 = LED - 5mm [color="Red (633nm)" package="5 mm [THT]"]
  LED9 = LED - 5mm [color="Red (633nm)" package="5 mm [THT]"]
  LED10 = LED - 5mm [color="Red (633nm)" package="5 mm [THT]"]
  LED11 = LED - 5mm [color="Red (633nm)" package="5 mm [THT]"]
  LED12 = LED - 5mm [color="Red (633nm)" package="5 mm [THT]"]
  LED13 = LED - 5mm [color="Red (633nm)" package="5 mm [THT]"]
  R1 = Resistor [tolerance=±5% resistance=220 package=THT]
  R2 = Resistor [tolerance=±5% resistance=220 package=THT]
  R3 = Resistor [tolerance=±5% resistance=220 package=THT]
  R4 = Resistor [tolerance=±5% resistance=220 package=THT]
  R5 = Resistor [tolerance=±5% resistance=220 package=THT]
  R6 = Resistor [tolerance=±5% resistance=220 package=THT]
  R7 = Resistor [tolerance=±5% resistance=220 package=THT]
  R8 = Resistor [tolerance=±5% resistance=220 package=THT]
  R9 = Resistor [tolerance=±5% resistance=220 package=THT]
  R10 = Resistor [tolerance=±5% resistance=220 package=THT]
  R11 = Resistor [tolerance=±5% resistance=220 package=THT]
  R12 = Resistor [tolerance=±5% resistance=220 package=THT]
  R13 = Resistor [tolerance=±5% resistance=220 package=THT]
  S1 = Pushbutton [package="[THT]"]
  S2 = Pushbutton [package="[THT]"]

nets:
  N1: Composant1.A0, Composant1.A5/SCL, Composant1.GND, LED1.anode, LED2.anode, LED3.anode, LED4.anode, LED5.anode, LED6.anode, LED7.anode, LED8.anode, LED9.anode, LED10.anode, LED11.anode, LED12.anode, LED13.anode, S1.Pin_1, S1.Pin_2, S2.Pin_1, S2.Pin_2
  N2: Composant1.D8, R6.Pin_1
  N3: Composant1.D9_PWM, R5.Pin_1
  N4: Composant1.D10_PWM/SS, R4.Pin_1
  N5: Composant1.D11_PWM/MOSI, R3.Pin_1
  N6: Composant1.D12/MISO, R2.Pin_1
  N7: Composant1.D13/SCK, R1.Pin_1
  N8: Composant1.D1/TX, R13.Pin_1
  N9: Composant1.D2, R12.Pin_1
  N10: Composant1.D3_PWM, R11.Pin_1
  N11: Composant1.D4, R10.Pin_1
  N12: Composant1.D5_PWM, R9.Pin_1
  N13: Composant1.D6_PWM, R8.Pin_1
  N14: Composant1.D7, R7.Pin_1
  N15: LED1.cathode, R1.Pin_0
  N16: LED2.cathode, R2.Pin_0
  N17: LED3.cathode, R3.Pin_0
  N18: LED4.cathode, R4.Pin_0
  N19: LED5.cathode, R5.Pin_0
  N20: LED6.cathode, R6.Pin_0
  N21: LED7.cathode, R7.Pin_0
  N22: LED8.cathode, R8.Pin_0
  N23: LED9.cathode, R9.Pin_0
  N24: LED10.cathode, R10.Pin_0
  N25: LED11.cathode, R11.Pin_0
  N26: LED12.cathode, R12.Pin_0
  N27: LED13.cathode, R13.Pin_0
  N28: S1.Pin_3, S1.Pin_4
  N29: S2.Pin_3, S2.Pin_4

notes:
  -----Heures------
  -------Minutes--------
  https://www.sla99.fr
